# Fritzing sketch rpi_ws2812_shield (saved by Fritzing 0.9.3b)
circuit board: 6.12146cm x 3.68701cm
perfboards: 1

parts:
  U1 = OP482 - Low Power, High Speed JFET Quad Operational Amplifier [part_number=OP482]
  Raspberry_Pi_1 = Raspberry Pi 3 [part_number=RPI-3-V1.2]  # not connected
  J2 = Power Jack [package=power_jack_pth_lock]
  J3 = Raspberry Pi Header 40pin [form="♂ (male)" package=THT]
  J4 = Camdenboss CTB0158-3 [part_number=CTB0158-3 package=THT]
  J5 = Camdenboss CTB0158-3 [part_number=CTB0158-3 package=THT]

nets:
  GND: U1.OUTA, U1.OUTB, J2.GND, J3.GND, J4.pin3, J5.pin3
  N1: U1.-INA, J3.GIPO18
  N2: U1.+INA, J5.pin2
  N3: U1.+IND, J4.pin2
  N4: U1.-IND, J3.GIPO13
  N5: U1.OUTD, J2.PWR, J3.5V, J4.pin1, J5.pin1

custom parts:
  Raspberry Pi Header 40pin: Raspberry Pi 40 pin header - for creating your own shields.
